// Logisim project Ctl_Conditional.circ as structural Verilog: 1 circuit, main circuit Conditional
module Conditional (
  input  Enable,
  input  [15:0] Instruction,
  input  Z,
  input  C,
  input  N,
  input  V,
  output [10:0] Offset,
  output Verified
);

  wire and_1_out, and_2_out, and_3_out, IS_Uncond, multiplexer_1_out, multiplexer_2_out, not_1_out,
       not_2_out, not_3_out, not_4_out, not_5_out, not_6_out, or_1_out, xnor_1_out;
  wire [10:0] bit_extender_1_out, bit_extender_2_out, multiplexer_3_out;

  not not_1 (not_1_out, Z);
  not not_2 (not_2_out, C);
  not not_3 (not_3_out, N);
  Comparator #(.width(5)) comparator_1 (.a(5'b11100), .b(Instruction[15:11]), .eq(IS_Uncond));  // open: gt, lt
  not not_4 (not_4_out, V);
  and and_1 (and_1_out, C, not_1_out);
  or or_1 (or_1_out, not_2_out, Z);
  xnor xnor_1 (xnor_1_out, N, V);
  and and_2 (and_2_out, not_1_out, xnor_1_out);
  and and_3 (and_3_out, Z, not_5_out);
  not not_5 (not_5_out, xnor_1_out);
  not not_6 (not_6_out, xnor_1_out);
  Multiplexer #(.select(4)) multiplexer_1 (
    .in0(Z), .in1(not_1_out), .in2(C), .in3(not_2_out), .in4(N), .in5(not_3_out), .in6(V), .in7(not_4_out),
    .in8(and_1_out), .in9(or_1_out), .in10(xnor_1_out), .in11(not_6_out), .in12(and_2_out), .in13(and_3_out),
    .in14(1'b1), .in15(1'b0), .out(multiplexer_1_out), .sel(Instruction[11:8]));
  assign bit_extender_1_out = {{3{Instruction[7]}}, Instruction[7:0]};  // Bit_Extender bit_extender_1
  Multiplexer multiplexer_2 (.in0(multiplexer_1_out), .in1(1'b1), .out(multiplexer_2_out), .sel(IS_Uncond));
  assign bit_extender_2_out = {{10{Enable}}, Enable};  // Bit_Extender bit_extender_2
  Multiplexer #(.width(11)) multiplexer_3 (
    .in0(bit_extender_1_out), .in1(Instruction[10:0]), .out(multiplexer_3_out), .sel(IS_Uncond));
  and and_4 (Verified, multiplexer_2_out, Enable);
  assign Offset = bit_extender_2_out & multiplexer_3_out;  // AND_Gate and_5, 11 bits wide

  // Other names for the same wires on the sheet: Cond[3:0] = Instruction[11:8]
endmodule
