// Logisim project Ctl_Load_Store.circ as structural Verilog: 1 circuit, main circuit Load_Store
module Load_Store (
  input  Enable,
  input  [15:0] Instruction,
  input  Clk,
  input  Reset,
  input  [31:0] Stack_Pointer,
  output Load,
  output PC_Hold,
  output Store,
  output [2:0] Rmd,
  output [31:0] RAM_Addr
);

  wire and_1_out, d_ff_1_q, d_ff_1_qn, not_1_out, not_2_out, or_1_out;
  wire [2:0] bit_extender_3_out;
  wire [31:0] adder_1_out, bit_extender_1_out, bit_extender_2_out;

  not not_1 (not_1_out, d_ff_1_q);
  and and_1 (and_1_out, not_1_out, Instruction[11]);
  not not_2 (not_2_out, Instruction[11]);
  assign bit_extender_1_out = {{24{Instruction[7]}}, Instruction[7:0]};  // Bit_Extender bit_extender_1
  D_Flip_Flop #(.trigger("falling")) d_ff_1 (
    .D(and_1_out), .clk(Clk), .Q(d_ff_1_q), .Qn(d_ff_1_qn), .reset(or_1_out));  // open: preset
  or or_1 (or_1_out, ~Enable, ~Instruction[11], Reset);  // OR_Gate
  and and_2 (Store, Enable, not_2_out);
  Adder #(.width(32)) adder_1 (.a(bit_extender_1_out), .b(Stack_Pointer), .out(adder_1_out));  // open: cin, cout
  and and_3 (Load, Enable, Instruction[11], d_ff_1_q);
  // Probe on d_ff_1_q
  and and_4 (PC_Hold, d_ff_1_qn, Instruction[11], Enable);
  assign RAM_Addr = adder_1_out & bit_extender_2_out;  // AND_Gate and_5, 32 bits wide
  assign bit_extender_2_out = {{31{Enable}}, Enable};  // Bit_Extender bit_extender_2
  assign bit_extender_3_out = {{2{Enable}}, Enable};  // Bit_Extender bit_extender_3
  assign Rmd = Instruction[10:8] & bit_extender_3_out;  // AND_Gate and_6, 3 bits wide

  // Other names for the same wires on the sheet: Imm8[7:0] = Instruction[7:0]; DEST[2:0] = Instruction[10:8];
  //   Code = Instruction[11]

  // Notes on the sheet:
  //   Instruction: pull=down
  //   Delay load and hold PC for 1 cycle for the RAM to send out requested data 
endmodule
