// Logisim project Ctl_Opcode_Decoder.circ as structural Verilog: 1 circuit, main circuit Opcode_Decoder
module Opcode_Decoder (
  input  [5:0] Opcode,
  input  in_2,
  output Shift,
  output Data_Processing,
  output Load_Store,
  output SP_Address,
  output Conditional
);

  wire decoder_1_out4, decoder_1_out5, decoder_1_out6, decoder_1_out7, decoder_1_out12, decoder_1_out13,
       decoder_1_out14, decoder_1_out15, decoder_1_out20, decoder_1_out21, decoder_1_out22, decoder_1_out23,
       not_1_out, not_2_out, not_3_out, or_1_out, or_2_out, or_3_out, or_4_out, or_5_out, or_6_out, or_7_out,
       or_8_out, or_9_out, seize;

  Decoder #(.select(5)) decoder_1 (
    .out4(decoder_1_out4), .out5(decoder_1_out5), .out6(decoder_1_out6), .out7(decoder_1_out7),
    .out12(decoder_1_out12), .out13(decoder_1_out13), .out14(decoder_1_out14), .out15(decoder_1_out15),
    .out16(seize), .out20(decoder_1_out20), .out21(decoder_1_out21), .out22(decoder_1_out22),
    .out23(decoder_1_out23), .sel(Opcode[4:0]), .en(in_2));  // open: out0, out1, out2, out3, out8, out9, out10, out11, out17, out18, out19, out24, out25, out26, out27, out28, out29, out30, out31
  or or_1 (or_1_out, decoder_1_out4, decoder_1_out5);
  or or_2 (or_2_out, decoder_1_out6, decoder_1_out7);
  or or_3 (or_3_out, decoder_1_out12, decoder_1_out13);
  or or_4 (or_4_out, decoder_1_out14, decoder_1_out15);
  or or_5 (or_5_out, decoder_1_out20, decoder_1_out21);
  or or_6 (or_6_out, decoder_1_out22, decoder_1_out23);
  not not_1 (not_1_out, Opcode[5]);
  and and_1 (Shift, not_1_out, not_2_out);
  not not_2 (not_2_out, Opcode[4]);
  not not_3 (not_3_out, Opcode[5]);
  and and_2 (Data_Processing, not_3_out, seize);
  and and_3 (Load_Store, Opcode[5], or_7_out);
  or or_7 (or_7_out, or_1_out, or_2_out);
  and and_4 (SP_Address, Opcode[5], or_8_out);
  or or_8 (or_8_out, or_3_out, or_4_out);
  and and_5 (Conditional, Opcode[5], or_9_out);
  or or_9 (or_9_out, or_5_out, or_6_out);

  // Other names for the same wires on the sheet: BeforeLastbit = Opcode[4]; Lastbit = Opcode[5]

  // Notes on the sheet:
  //   Shift, add, sub, mov
  //   Load/Store
  //   SP Address
  //   Conditional branch
  //   Data Processing
endmodule
