// Logisim project Ctl_SP_Address.circ as structural Verilog: 1 circuit, main circuit SP_Address
module SP_Address (
  input  [15:0] Instruction,
  input  [31:0] Stack_Pointer,
  input  Enable,
  output [31:0] New_Stack_Pointer,
  output Write_Enable
);

  wire select_add_sub;
  wire [6:0] Imm7;
  wire [15:0] bit_extender_1_out;
  wire [15:8] and_1_out;
  wire [31:0] add, bit_extender_2_out, bit_extender_3_out, bit_extender_4_out, multiplexer_1_out, sub;

  assign bit_extender_1_out = {{15{Enable}}, Enable};  // Bit_Extender bit_extender_1
  assign bit_extender_2_out = {{25{Imm7[6]}}, Imm7};  // Bit_Extender bit_extender_2
  assign bit_extender_3_out = {{25{Imm7[6]}}, Imm7};  // Bit_Extender bit_extender_3
  assign {and_1_out, select_add_sub, Imm7} = bit_extender_1_out & Instruction;  // AND_Gate and_1, 16 bits wide
  Adder #(.width(32)) adder_1 (.a(bit_extender_2_out), .b(Stack_Pointer), .out(add));  // open: cin, cout
  Subtractor #(.width(32)) subtractor_1 (.a(bit_extender_3_out), .b(Stack_Pointer), .out(sub));  // open: bin, bout
  Multiplexer #(.width(32)) multiplexer_1 (.in0(add), .in1(sub), .out(multiplexer_1_out), .sel(select_add_sub));
  assign bit_extender_4_out = {{31{Enable}}, Enable};  // Bit_Extender bit_extender_4
  assign New_Stack_Pointer = multiplexer_1_out & bit_extender_4_out;  // AND_Gate and_2, 32 bits wide

  assign Write_Enable = Enable;

  // Other names for the same wires on the sheet: Stack_In[31:0] = Stack_Pointer

  // Notes on the sheet:
  //   Pull output low on Enable = 0
endmodule
