// Logisim project Ctl_Shift_Add_Sub_Mov.circ as structural Verilog: 1 circuit, main circuit Shift_Add_Sub_Mov
module Shift_Add_Sub_Mov (
  input  [15:0] Instruction,
  input  Enable,
  output Carry,
  output [3:0] Flags_Update_Mask,
  output Imm32_Enable,
  output [2:0] Rm,
  output [2:0] Rn,
  output [2:0] Rd,
  output [4:0] Imm5,
  output [31:0] Imm32,
  output [3:0] ALU_Opcode
);

  wire decoder_1_out0, decoder_1_out1, decoder_1_out2, decoder_1_out3, decoder_1_out4, decoder_1_out5,
       decoder_1_out6, decoder_1_out7, decoder_1_out8, decoder_1_out9, decoder_1_out10, decoder_1_out11,
       decoder_1_out16, decoder_1_out17, decoder_1_out18, decoder_1_out19, decoder_1_out20, decoder_1_out21,
       decoder_1_out22, decoder_1_out23, decoder_1_out24, decoder_1_out25, decoder_1_out26, decoder_1_out27,
       decoder_1_out28, decoder_1_out29, decoder_1_out30, decoder_1_out31, IS_RD1, IS_RD2, IS_RD3, IS_RD4,
       IS_RD5, isADDImme, isADDImmeHuit, isADDReg, isASR, isCmp, isLSL, isLSR, isSUBImme, isSUBImmeHuit,
       isSUBReg, or_1_out, or_2_out, or_13_out, or_14_out;
  wire [2:0] bit_extender_16_out, bit_extender_17_out, Imm3, multiplexer_2_out, multiplexer_3_out,
       priority_encoder_1_out, priority_encoder_2_out, RD1, RD2, RD3, RD4, RD5, RM_t, RN1, RN2, RN3;
  wire [3:0] and_1_out, and_2_out, and_3_out, and_6_out, and_7_out, and_8_out, and_9_out, and_10_out,
       and_11_out, and_12_out, bit_extender_1_out, bit_extender_2_out, bit_extender_3_out,
       bit_extender_6_out, bit_extender_7_out, bit_extender_8_out, bit_extender_9_out, bit_extender_10_out,
       bit_extender_11_out, bit_extender_12_out;
  wire [15:0] and_13_out, and_14_out, bit_extender_4_out, bit_extender_5_out, bit_extender_13_out,
       bit_extender_14_out, bit_extender_15_out;
  wire [15:9] and_4_out, and_15_out;
  wire [15:11] and_5_out;
  wire [31:0] Imm8, negator_1_out;

  Decoder #(.select(5)) decoder_1 (
    .out0(decoder_1_out0), .out1(decoder_1_out1), .out2(decoder_1_out2), .out3(decoder_1_out3),
    .out4(decoder_1_out4), .out5(decoder_1_out5), .out6(decoder_1_out6), .out7(decoder_1_out7),
    .out8(decoder_1_out8), .out9(decoder_1_out9), .out10(decoder_1_out10), .out11(decoder_1_out11),
    .out12(isADDReg), .out13(isSUBReg), .out14(isADDImme), .out15(isSUBImme), .out16(decoder_1_out16),
    .out17(decoder_1_out17), .out18(decoder_1_out18), .out19(decoder_1_out19), .out20(decoder_1_out20),
    .out21(decoder_1_out21), .out22(decoder_1_out22), .out23(decoder_1_out23), .out24(decoder_1_out24),
    .out25(decoder_1_out25), .out26(decoder_1_out26), .out27(decoder_1_out27), .out28(decoder_1_out28),
    .out29(decoder_1_out29), .out30(decoder_1_out30), .out31(decoder_1_out31), .sel(Instruction[13:9]),
    .en(Enable));
  assign bit_extender_1_out = {{3{or_1_out}}, or_1_out};  // Bit_Extender bit_extender_1
  or or_1 (or_1_out, isLSL, isLSR, isASR);
  assign bit_extender_2_out = {{3{or_2_out}}, or_2_out};  // Bit_Extender bit_extender_2
  or or_2 (or_2_out, isADDReg, isSUBReg, isADDImme, isSUBImme, isCmp, isADDImmeHuit, isSUBImmeHuit);
  assign bit_extender_3_out = {{3{IS_RD4}}, IS_RD4};  // Bit_Extender bit_extender_3
  assign and_1_out = bit_extender_1_out & 4'b1110;  // AND_Gate and_1, 4 bits wide
  assign and_2_out = bit_extender_2_out & 4'b1111;  // AND_Gate and_2, 4 bits wide
  assign and_3_out = bit_extender_3_out & 4'b1100;  // AND_Gate and_3, 4 bits wide
  assign Flags_Update_Mask = and_1_out | and_2_out | and_3_out;  // OR_Gate or_3, 4 bits wide
  or or_4 (isLSL, decoder_1_out0, decoder_1_out1, decoder_1_out2, decoder_1_out3);
  or or_5 (isLSR, decoder_1_out4, decoder_1_out5, decoder_1_out6, decoder_1_out7);
  or or_6 (isASR, decoder_1_out8, decoder_1_out9, decoder_1_out10, decoder_1_out11);
  or or_7 (IS_RD4, decoder_1_out16, decoder_1_out17, decoder_1_out18, decoder_1_out19);
  or or_8 (isCmp, decoder_1_out20, decoder_1_out21, decoder_1_out22, decoder_1_out23);
  or or_9 (isADDImmeHuit, decoder_1_out24, decoder_1_out25, decoder_1_out26, decoder_1_out27);
  or or_10 (isSUBImmeHuit, decoder_1_out28, decoder_1_out29, decoder_1_out30, decoder_1_out31);
  or or_11 (IS_RD1, isADDImme, isSUBImme);
  or or_12 (IS_RD2, isLSL, isLSR, isASR);
  assign bit_extender_4_out = {{15{IS_RD1}}, IS_RD1};  // Bit_Extender bit_extender_4
  assign {and_4_out, Imm3, RN1, RD1} = bit_extender_4_out & Instruction;  // AND_Gate and_4, 16 bits wide
  assign bit_extender_5_out = {{15{IS_RD2}}, IS_RD2};  // Bit_Extender bit_extender_5
  assign {and_5_out, Imm5, RN2, RD2} = bit_extender_5_out & Instruction;  // AND_Gate and_5, 16 bits wide
  assign bit_extender_6_out = {{3{or_13_out}}, or_13_out};  // Bit_Extender bit_extender_6
  or or_13 (or_13_out, isADDReg, isADDImme, isADDImmeHuit);
  assign bit_extender_7_out = {{3{or_14_out}}, or_14_out};  // Bit_Extender bit_extender_7
  or or_14 (or_14_out, isSUBReg, isSUBImme, isSUBImmeHuit);
  assign bit_extender_8_out = {{3{IS_RD4}}, IS_RD4};  // Bit_Extender bit_extender_8
  assign bit_extender_9_out = {{3{isCmp}}, isCmp};  // Bit_Extender bit_extender_9
  assign bit_extender_10_out = {{3{isLSL}}, isLSL};  // Bit_Extender bit_extender_10
  assign bit_extender_11_out = {{3{isLSR}}, isLSR};  // Bit_Extender bit_extender_11
  assign bit_extender_12_out = {{3{isASR}}, isASR};  // Bit_Extender bit_extender_12
  assign and_6_out = bit_extender_6_out & 4'b0101;  // AND_Gate and_6, 4 bits wide
  assign and_7_out = bit_extender_7_out & 4'b0110;  // AND_Gate and_7, 4 bits wide
  assign and_8_out = bit_extender_8_out & 4'b1001;  // AND_Gate and_8, 4 bits wide
  assign and_9_out = bit_extender_9_out & 4'b1010;  // AND_Gate and_9, 4 bits wide
  or or_15 (IS_RD3, isSUBImmeHuit, isCmp, isADDImmeHuit);
  or or_16 (IS_RD5, isADDReg, isSUBReg);
  assign and_10_out = bit_extender_10_out & 4'b0010;  // AND_Gate and_10, 4 bits wide
  assign and_11_out = bit_extender_11_out & 4'b0011;  // AND_Gate and_11, 4 bits wide
  assign and_12_out = bit_extender_12_out & 4'b0100;  // AND_Gate and_12, 4 bits wide
  assign bit_extender_13_out = {{15{IS_RD3}}, IS_RD3};  // Bit_Extender bit_extender_13
  assign {and_13_out[15:11], RD3, and_13_out[7:0]} = bit_extender_13_out & Instruction;  // AND_Gate and_13, 16 bits wide
  assign {and_14_out[15:11], RD4, and_14_out[7:0]} = bit_extender_14_out & Instruction;  // AND_Gate and_14, 16 bits wide
  assign bit_extender_14_out = {{15{IS_RD4}}, IS_RD4};  // Bit_Extender bit_extender_14
  assign bit_extender_15_out = {{15{IS_RD5}}, IS_RD5};  // Bit_Extender bit_extender_15
  assign {and_15_out, RM_t, RN3, RD5} = bit_extender_15_out & Instruction;  // AND_Gate and_15, 16 bits wide
  assign ALU_Opcode = and_10_out | and_11_out | and_12_out | and_6_out | and_7_out | and_8_out | and_9_out;  // OR_Gate or_17, 4 bits wide
  Negator #(.width(32)) negator_1 (.in({{24{1'b0}}, and_14_out[7:0]}), .out(negator_1_out));
  Multiplexer #(.width(32)) multiplexer_1 (
    .in0({{24{1'b0}}, and_13_out[7:0]}), .in1(negator_1_out), .out(Imm8), .sel(IS_RD4));
  Priority_Encoder priority_encoder_1 (
    .in0(IS_RD1), .in1(IS_RD2), .in2(IS_RD3), .in3(IS_RD4), .in4(IS_RD5), .in5(1'b0), .in6(1'b0), .in7(1'b0),
    .out(priority_encoder_1_out));  // open: en_in, gs, en_out
  Priority_Encoder priority_encoder_2 (
    .in0(IS_RD1), .in1(IS_RD2), .in2(IS_RD3), .in3(IS_RD4), .in4(IS_RD5), .in5(1'b0), .in6(1'b0), .in7(1'b0),
    .out(priority_encoder_2_out));  // open: en_in, gs, en_out
  or or_18 (Carry, isSUBReg, isSUBImme, isSUBImmeHuit);
  or or_19 (Imm32_Enable, isADDImmeHuit, isADDImme, IS_RD4, isCmp, isSUBImme, isSUBImmeHuit);
  assign Rm = RM_t | RN2;  // OR_Gate or_20, 3 bits wide
  assign bit_extender_16_out = {{2{Enable}}, Enable};  // Bit_Extender bit_extender_16
  Multiplexer #(.select(3), .width(3)) multiplexer_2 (
    .in0(RD1), .in1(RD2), .in2(RD3), .in3(RD4), .in4(RD5), .in5(3'b000), .in6(3'b000), .in7(3'b000),
    .out(multiplexer_2_out), .sel(priority_encoder_1_out));
  Multiplexer #(.select(3), .width(3)) multiplexer_3 (
    .in0(RN1), .in1(RN2), .in2(RD3), .in3(3'b000), .in4(RN3), .in5(3'b000), .in6(3'b000), .in7(3'b000),
    .out(multiplexer_3_out), .sel(priority_encoder_2_out));
  assign Imm32 = {{29{1'b0}}, Imm3} | Imm8;  // OR_Gate or_21, 32 bits wide
  assign Rd = bit_extender_16_out & multiplexer_2_out;  // AND_Gate and_16, 3 bits wide
  assign bit_extender_17_out = {{2{Enable}}, Enable};  // Bit_Extender bit_extender_17
  assign Rn = bit_extender_17_out & multiplexer_3_out;  // AND_Gate and_17, 3 bits wide

  // Other names for the same wires on the sheet: Flags[3:0] = Flags_Update_Mask; In_put[15:0] = Instruction;
  //   isMov = IS_RD4; OPCode[3:0] = ALU_Opcode

  // Notes on the sheet:
  //   Pull output low on Enable = 0
  //   Note 3: Imm32_Enable forces the use of the immediate for Rm register
  //   Note: ALU uses Rn register for shifts. Use Rn instead of Rm for shifts (immediate) here too
  //   Note 2: MOV uses RSB ALU opcode with Imm8 reversed so that it is copied to output register
  //   0010
  //   flag 0111
  //   0011
  //   flag 0111
  //   0100
  //   flag 0111
  //   flag 0011
  //   1010
  //   0101
  //   0110
  //   flag 1111
  //   flag 1111
  //   flag 1111
  //   Enable carry for SUB since it is reversed in ALU
  //   ALU will use Imm32 instead of Rm
  //   only ADD and SUB use Rm
endmodule
